# Fritzing sketch controller__board (saved by Fritzing 0.9.3b)
stripboards: 1

parts:
  ESP32_-_Back1 = ESP32 - CAM
  JP1 = Grove Header 4pin Straight direct mount [package=straight]
  JP2 = Grove Header 4pin Straight direct mount [package=straight]
  JP3 = Grove Header 4pin Straight direct mount [package=straight]
  JP4 = Grove Header 4pin Straight direct mount [package=straight]

nets:
  N1: ESP32_-_Back1.GPIO4, ESP32_-_Back1.GND#16
  N2: ESP32_-_Back1.GPIO2, ESP32_-_Back1.GPIO1_/_TX
  N3: ESP32_-_Back1.GPIO14, ESP32_-_Back1.GPIO3_/_RX
  N4: ESP32_-_Back1.GPIO15, ESP32_-_Back1.3.3V_/_5V_/_P_OUT
  N5: ESP32_-_Back1.GPIO13, ESP32_-_Back1.GND#12
  N6: ESP32_-_Back1.GPIO12, ESP32_-_Back1.GPIO0
  N7: ESP32_-_Back1.GND#7, ESP32_-_Back1.GPIO16
  5V: ESP32_-_Back1.5V, ESP32_-_Back1.3.3V
  N8: JP1.1, JP1.2, JP1.3, JP1.4, JP2.1, JP2.2, JP2.3, JP2.4
  N9: JP3.1, JP3.2, JP3.3, JP3.4, JP4.1, JP4.2, JP4.3, JP4.4

custom parts:
  ESP32 - CAM: The ESP32-CAM has a very competitive small-size camera module that can operate independently as a minimum system with a footprint of only 27*40.5*4.5mm and a deep sleep current of up to 6mA.
  Grove Header 4pin Straight direct mount: Header
