# Fritzing sketch main__board__v1 (saved by Fritzing 0.9.3b)

parts:
  ESP32_-_Back1 = ESP32 - CAM
  Header1 = 2 pin header [package=THT]
  Header2 = 2 pin header [package=THT]
  Header3 = 2 pin header [package=THT]
  Header4 = 2 pin header [package=THT]
  Header5 = 2 pin header [package=THT]
  Header6 = 2 pin header [package=THT]
  Header7 = 2 pin header [package=THT]
  Header9 = 2 pin header [package=THT]
  Header11 = 2 pin header [package=THT]
  Header12 = 2 pin header [package=THT]
  SW1 = Slide_Switch_new
  VCC1 = Battery
  L298N1 = L298N DC motor driver
  SW2 = Slide_Switch_new
  M1 = DC Motor
  M2 = DC Motor
  Header13 = 2 pin header [package=THT]
  LED2 = LED - 5mm [color="Yellow (595nm)" package="5 mm [THT]"]
  LED3 = LED - 5mm [color="Yellow (595nm)" package="5 mm [THT]"]
  LED4 = LED - 5mm [color="White (4500K)" package="5 mm [THT]"]
  LED5 = LED - 5mm [color="Yellow (595nm)" package="5 mm [THT]"]
  LED6 = LED - 5mm [color="Yellow (595nm)" package="5 mm [THT]"]
  LED7 = LED - 5mm [color="Red (633nm)" package="5 mm [THT]"]
  LED8 = LED - 5mm [color="Red (633nm)" package="5 mm [THT]"]
  LED10 = LED - 5mm [color="White (4500K)" package="5 mm [THT]"]
  R1 = Resistor [tolerance=±5% resistance=220 package="0402 [SMD]"]
  R2 = Resistor [tolerance=±5% resistance=220 package="0402 [SMD]"]
  R3 = Resistor [tolerance=±5% resistance=220 package="0402 [SMD]"]
  R4 = Resistor [tolerance=±5% resistance=220 package="0402 [SMD]"]
  Header14 = 2 pin header [package=THT]
  Header15 = 2 pin header [package=THT]
  Header16 = 2 pin header [package=THT]
  Header17 = 2 pin header [package=THT]
  Header18 = 2 pin header [package=THT]
  Header19 = 2 pin header [package=THT]
  R5 = Resistor [tolerance=±5% resistance=220 package="0402 [SMD]"]
  R6 = Resistor [tolerance=±5% resistance=220 package="0402 [SMD]"]
  R7 = Resistor [tolerance=±5% resistance=220 package="0402 [SMD]"]
  R8 = Resistor [tolerance=±5% resistance=220 package="0402 [SMD]"]

nets:
  N1: ESP32_-_Back1.GPIO4, Header6.pin_1#0
  N2: ESP32_-_Back1.GPIO2, Header6.pin_1#1
  N3: ESP32_-_Back1.GPIO14, Header5.pin_1#0
  N4: ESP32_-_Back1.GPIO15, Header5.pin_1#1
  N5: ESP32_-_Back1.GPIO13, Header4.pin_1#0
  N6: ESP32_-_Back1.GPIO12, Header4.pin_1#1
  N7: ESP32_-_Back1.GND#7, Header12.pin_1#1, LED3.cathode, LED10.cathode
  N8: ESP32_-_Back1.5V, Header12.pin_1#0
  N9: ESP32_-_Back1.GPIO16, Header7.pin_1
  N10: ESP32_-_Back1.GPIO0, Header14.pin_1
  N11: ESP32_-_Back1.3.3V_/_5V_/_P_OUT, Header11.pin_1#1
  N12: ESP32_-_Back1.GPIO3_/_RX, Header17.pin_1
  N13: ESP32_-_Back1.GPIO1_/_TX, Header18.pin_1
  N14: ESP32_-_Back1.GND#16, Header11.pin_1#0, LED2.cathode, LED4.cathode, LED6.cathode, LED8.cathode
  N15: Header1.pin_1#0, L298N1.ENB
  N16: Header1.pin_1#1, L298N1.IN4
  N17: Header2.pin_1#0, L298N1.IN3
  N18: Header2.pin_1#1, L298N1.IN2
  N19: Header3.pin_1#0, L298N1.IN1
  N20: Header3.pin_1#1, L298N1.ENA
  N21: Header9.pin_1#0, R6.Pin_0
  N22: Header9.pin_1#1, R1.Pin_0
  N23: SW1.pin_1, L298N1.5V
  N24: SW1.pin_2, Header13.pin_1#0
  N25: VCC1.-, L298N1.GND, Header13.pin_1#1, LED5.cathode, LED7.cathode
  N26: VCC1.+, SW2.pin_1
  N27: L298N1.OUT1, M1.pin_2
  N28: L298N1.OUT2, M1.pin_1
  N29: L298N1.OUT3, M2.pin_2
  N30: L298N1.OUT4, M2.pin_1
  N31: L298N1.12V, SW2.pin_2
  N32: LED2.anode, R3.Pin_1
  N33: LED3.anode, R1.Pin_1
  N34: LED4.anode, R2.Pin_1
  N35: LED5.anode, R6.Pin_1
  N36: LED6.anode, R8.Pin_1
  N37: LED7.anode, R5.Pin_1
  N38: LED8.anode, R7.Pin_1
  N39: LED10.anode, R4.Pin_1
  N40: R2.Pin_0, Header19.pin_1#0
  N41: R3.Pin_0, Header15.pin_1#0
  N42: R4.Pin_0, Header19.pin_1#1
  N43: Header15.pin_1#1, R8.Pin_0
  N44: Header16.pin_1#0, R7.Pin_0
  N45: Header16.pin_1#1, R5.Pin_0

custom parts:
  ESP32 - CAM: The ESP32-CAM has a very competitive small-size camera module that can operate independently as a minimum system with a footprint of only 27*40.5*4.5mm and a deep sleep current of up to 6mA.
  2 pin header: 2 pin male to male header
  Slide_Switch_new: the New two pin slide switch
  L298N DC motor driver: 2x DC motor driver with 78M05 positive voltage regulator (7..35 V) L298N: max 46 V, 2 A Set 5 V Enable jumper to enable 5 V regultor (needed for the L298N) and +5 V output at screw terminal or supply external +5 V at screw terminal Set ENA and/or ENB to +5 V to enable motor permanently or supply ENA and/or ENB with PWM signal IN1 and IN2 set rotation directory for motor A (OUT1/OUT2) IN2 and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
