# Fritzing sketch main__board__v2 (saved by Fritzing 0.9.3b)

parts:
  ESP32-CAM = ESP32 - CAM
  Header12 = 2 pin header [package=THT]
  SWITCH_2 = Slide_Switch_new
  BATTERIES = Battery
  L298N = L298N DC motor driver
  SWITCH_1 = Slide_Switch_new
  DC_MOTOR_1 = DC Motor
  DC_MOTOR_2 = DC Motor
  Header13 = 2 pin header [package=THT]
  ESP32-WROOM_32 = ESP32S-HiLetgo [part_number=ESP32S-HiLetgo]
  MPU6050 = InvenSense MPU6050
  HC-SR04 = HC-SR04 Ultrasonic Distance Sensor
  LED1 = smd LED [color="Red (633nm)" package="0603 [SMD]"]
  LED2 = smd LED [color="Red (633nm)" package="0603 [SMD]"]
  LED3 = smd LED [color="White (4500K)" package="0603 [SMD]"]
  LED4 = smd LED [color="White (4500K)" package="0603 [SMD]"]
  LED5 = smd LED [color="Yellow (595nm)" package="0603 [SMD]"]
  LED6 = smd LED [color="Yellow (595nm)" package="0603 [SMD]"]
  LED7 = smd LED [color="Yellow (595nm)" package="0603 [SMD]"]
  LED8 = smd LED [color="Yellow (595nm)" package="0603 [SMD]"]
  R1 = Resistor [tolerance=±5% resistance=220 package="2512 [SMD]"]
  R2 = Resistor [tolerance=±5% resistance=220 package="2512 [SMD]"]
  R3 = Resistor [tolerance=±5% resistance=220 package="2512 [SMD]"]
  R4 = Resistor [tolerance=±5% resistance=220 package="2512 [SMD]"]
  R5 = Resistor [tolerance=±5% resistance=220 package="2512 [SMD]"]
  R6 = Resistor [tolerance=±5% resistance=220 package="2512 [SMD]"]
  R7 = Resistor [tolerance=±5% resistance=220 package="2512 [SMD]"]
  R8 = Resistor [tolerance=±5% resistance=220 package="2512 [SMD]"]

nets:
  N1: ESP32-CAM.GPIO12, ESP32-CAM.GND, Header12.pin_1#1
  N2: ESP32-CAM.5V, Header12.pin_1#0
  N3: SWITCH_2.pin_1, L298N.5V
  VCC: SWITCH_2.pin_2, Header13.pin_1#0, ESP32-WROOM_32.VIN, MPU6050.VCC, HC-SR04.VCC
  GND: BATTERIES.-, L298N.GND, Header13.pin_1#1, ESP32-WROOM_32.GND, MPU6050.GND, HC-SR04.GND, LED1.cathode, LED2.cathode, LED3.cathode, LED4.cathode, LED5.cathode, LED6.cathode, LED7.cathode, LED8.cathode
  N4: BATTERIES.+, SWITCH_1.pin_1
  N5: L298N.OUT1, DC_MOTOR_1.pin_2
  N6: L298N.OUT2, DC_MOTOR_1.pin_1
  N7: L298N.OUT3, DC_MOTOR_2.pin_2
  N8: L298N.OUT4, DC_MOTOR_2.pin_1
  N9: L298N.12V, SWITCH_1.pin_2
  N10: L298N.ENA, ESP32-WROOM_32.GPIO15
  N11: L298N.ENB, ESP32-WROOM_32.GPIO17
  N12: L298N.IN1, ESP32-WROOM_32.GPIO2
  N13: L298N.IN2, ESP32-WROOM_32.GPIO0
  N14: L298N.IN3, ESP32-WROOM_32.GPIO16
  N15: L298N.IN4, ESP32-WROOM_32.GPIO4
  N16: ESP32-WROOM_32.GPIO12, R3.Pin_0, R4.Pin_0
  N17: ESP32-WROOM_32.GPIO13, HC-SR04.ECHO
  N18: ESP32-WROOM_32.GPIO9, HC-SR04.TRIG
  N19: ESP32-WROOM_32.GPIO6, R7.Pin_0, R8.Pin_1
  N20: ESP32-WROOM_32.GPIO18, R1.Pin_1, R2.Pin_1
  N21: ESP32-WROOM_32.GPIO19, R5.Pin_1, R6.Pin_0
  N22: ESP32-WROOM_32.GPIO21, MPU6050.XCL
  N23: ESP32-WROOM_32.GPIO3, MPU6050.XDA
  N24: ESP32-WROOM_32.GPIO1, MPU6050.SDA
  N25: ESP32-WROOM_32.GPIO22, MPU6050.SCL
  N26: LED1.anode, R1.Pin_0
  N27: LED2.anode, R2.Pin_0
  N28: LED3.anode, R4.Pin_1
  N29: LED4.anode, R3.Pin_1
  N30: LED5.anode, R8.Pin_0
  N31: LED6.anode, R5.Pin_0
  N32: LED7.anode, R6.Pin_1
  N33: LED8.anode, R7.Pin_1

notes:
  ESP32-CAM Power
  Video Stream Only

custom parts:
  ESP32 - CAM: The ESP32-CAM has a very competitive small-size camera module that can operate independently as a minimum system with a footprint of only 27*40.5*4.5mm and a deep sleep current of up to 6mA.
  2 pin header: 2 pin male to male header
  Slide_Switch_new: the New two pin slide switch
  L298N DC motor driver: 2x DC motor driver with 78M05 positive voltage regulator (7..35 V) L298N: max 46 V, 2 A Set 5 V Enable jumper to enable 5 V regultor (needed for the L298N) and +5 V output at screw terminal or supply external +5 V at screw terminal Set ENA and/or ENB to +5 V to enable motor permanently or supply ENA and/or ENB with PWM signal IN1 and IN2 set rotation directory for motor A (OUT1/OUT2) IN2 and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
  ESP32S-HiLetgo: HiLetgo ESP-WROOM-32 ESP32 ESP-32S Development Board 2.4GHz Dual-Mode WiFi + Bluetooth Dual Cores Microcontroller The ESP32 integrated with Antenna switches, RF Balun, power amplifiers, low-noise amplifiers, filters, and management modules, and the entire solution occupies the least area of PCB. 2.4 GHz Wi-Fi plus Bluetooth dual-mode chip, with TSMC Ultra-low power consumption 40nm technology,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
